// Logisim project Addition-Subtraction.circ as structural Verilog: 8 circuits, main circuit Adder/ Subtractor
module Adder__Subtractor (
  input  B4,
  input  B3,
  input  B2,
  input  B1,
  input  B0,
  input  A4,
  input  A3,
  input  A2,
  input  A1,
  input  A0,
  input  _0__Add,
  output R4,
  output R3,
  output R2,
  output R1,
  output R0,
  output Sign
);

  wire n5bitadder_1_s0, n5bitadder_1_s1, n5bitadder_1_s2, n5bitadder_1_s3, n5th_bit_handler_1_out_4,
       selective_2_s_complement_4bits_1_carry, selective_2_s_complement_4bits_1_complement0,
       selective_2_s_complement_4bits_1_complement1, selective_2_s_complement_4bits_1_complement2,
       selective_2_s_complement_4bits_1_complement3, selective_2_s_complement_4bits_2_carry;
  wire [1:1] n5bitadder_1_s4;
  wire [4:0] selective_2_s_complement_4bits_3_complement0, xor_5_out;

  Indicator indicator_1 (.M(_0__Add), .fifthbit(n5bitadder_1_s4[1]), .s1(A4), .s2(B4), .indactor(Sign));
  _5th_Bit_Handler u_5th_bit_handler_1 (
    .fifthbit(n5bitadder_1_s4[1]), .s1(A4), .s2(B4), .out_4(n5th_bit_handler_1_out_4));
  xor xor_1 (xor_5_out[3], _0__Add, selective_2_s_complement_4bits_1_complement3);
  xor xor_2 (xor_5_out[4], selective_2_s_complement_4bits_1_carry, _0__Add);
  xor xor_3 (xor_5_out[1], _0__Add, selective_2_s_complement_4bits_1_complement1);
  xor xor_4 (xor_5_out[2], _0__Add, selective_2_s_complement_4bits_1_complement2);
  Selective_2_s_Complement_4bits selective_2_s_complement_4bits_1 (
    .no0(B0), .sign(B4), .Carry_in(B4), .no1(B1), .no2(B2), .no3(B3), .sign_2(B4), .sign_3(B4), .sign_4(B4),
    .complement0(selective_2_s_complement_4bits_1_complement0),
    .complement1(selective_2_s_complement_4bits_1_complement1),
    .complement2(selective_2_s_complement_4bits_1_complement2),
    .complement3(selective_2_s_complement_4bits_1_complement3), .Carry(selective_2_s_complement_4bits_1_carry));
  xor xor_5 (xor_5_out[0], _0__Add, selective_2_s_complement_4bits_1_complement0);
  _5BitAdder u_5bitadder_1 (
    .cin(_0__Add), .b4(xor_5_out[4]), .b3(xor_5_out[3]), .b2(xor_5_out[2]), .b1(xor_5_out[1]),
    .b0(xor_5_out[0]), .a4(selective_2_s_complement_4bits_3_complement0[4]),
    .a3(selective_2_s_complement_4bits_3_complement0[3]),
    .a2(selective_2_s_complement_4bits_3_complement0[2]),
    .a1(selective_2_s_complement_4bits_3_complement0[1]),
    .a0(selective_2_s_complement_4bits_3_complement0[0]), .s4(n5bitadder_1_s4[1]), .s3(n5bitadder_1_s3),
    .s2(n5bitadder_1_s2), .s1(n5bitadder_1_s1), .s0(n5bitadder_1_s0));  // open: c4
  Selective_2_s_Complement_1bit selective_2_s_complement_1bit_1 (
    .no(n5th_bit_handler_1_out_4), .sign(Sign), .Carry_in(selective_2_s_complement_4bits_2_carry),
    .complement(R4));  // open: Carry
  Selective_2_s_Complement_4bits selective_2_s_complement_4bits_2 (
    .no0(n5bitadder_1_s0), .sign(Sign), .Carry_in(Sign), .no1(n5bitadder_1_s1), .no2(n5bitadder_1_s2),
    .no3(n5bitadder_1_s3), .sign_2(Sign), .sign_3(Sign), .sign_4(Sign), .complement0(R0), .complement1(R1),
    .complement2(R2), .complement3(R3), .Carry(selective_2_s_complement_4bits_2_carry));
  Selective_2_s_Complement_4bits selective_2_s_complement_4bits_3 (
    .no0(A0), .sign(A4), .Carry_in(A4), .no1(A1), .no2(A2), .no3(A3), .sign_2(A4), .sign_3(A4), .sign_4(A4),
    .complement0(selective_2_s_complement_4bits_3_complement0[0]),
    .complement1(selective_2_s_complement_4bits_3_complement0[1]),
    .complement2(selective_2_s_complement_4bits_3_complement0[2]),
    .complement3(selective_2_s_complement_4bits_3_complement0[3]),
    .Carry(selective_2_s_complement_4bits_3_complement0[4]));

  // Notes on the sheet:
  //   Sign 0: Postive
  //   Sign 1: Negative
  //   Adding Equation : A+B
  //   Subratcion Equation : A + B' +1 
  //   1: Subtract
endmodule

// 2's
module Selective_2_s_Complement_1bit (
  input  no,
  input  sign,
  input  Carry_in,
  output complement,
  output Carry
);

  wire xor_1_out;

  xor xor_1 (xor_1_out, no, sign);
  FullAdder fulladder_1 (.X(xor_1_out), .Y(Carry_in), .C_IN(1'b0), .SUM(complement), .C_OUT(Carry));
endmodule

module FullAdder (
  input  X,
  input  Y,
  input  C_IN,
  output SUM,
  output C_OUT
);

  wire and_1_out, and_2_out, xor_1_out;

  xor xor_1 (xor_1_out, X, Y);
  and and_1 (and_1_out, X, Y);
  and and_2 (and_2_out, xor_1_out, C_IN);
  xor xor_2 (SUM, xor_1_out, C_IN);
  or or_1 (C_OUT, and_2_out, and_1_out);

  // Notes on the sheet:
  //   Full Adder
endmodule

// Selective 2's Comp
module Selective_2_s_Complement_4bits (
  input  no0,
  input  sign,
  input  Carry_in,
  input  no1,
  input  no2,
  input  no3,
  input  sign_2,
  input  sign_3,
  input  sign_4,
  output complement0,
  output complement1,
  output complement2,
  output complement3,
  output Carry
);

  wire fulladder_1_c_out, fulladder_2_c_out, fulladder_3_c_out, xor_1_out, xor_2_out, xor_3_out, xor_4_out;

  xor xor_1 (xor_1_out, no0, sign);
  xor xor_2 (xor_2_out, no1, sign_2);
  xor xor_3 (xor_3_out, no2, sign_3);
  xor xor_4 (xor_4_out, no3, sign_4);
  FullAdder fulladder_1 (.X(xor_1_out), .Y(Carry_in), .C_IN(1'b0), .SUM(complement0), .C_OUT(fulladder_1_c_out));
  FullAdder fulladder_2 (
    .X(xor_2_out), .Y(fulladder_1_c_out), .C_IN(1'b0), .SUM(complement1), .C_OUT(fulladder_2_c_out));
  FullAdder fulladder_3 (
    .X(xor_3_out), .Y(fulladder_2_c_out), .C_IN(1'b0), .SUM(complement2), .C_OUT(fulladder_3_c_out));
  FullAdder fulladder_4 (.X(xor_4_out), .Y(fulladder_3_c_out), .C_IN(1'b0), .SUM(complement3), .C_OUT(Carry));
endmodule

module _5BitAdder (
  input  a4,
  input  a3,
  input  a2,
  input  a1,
  input  a0,
  input  b4,
  input  b3,
  input  b2,
  input  b1,
  input  b0,
  input  cin,
  output c4,
  output s4,
  output s3,
  output s1,
  output s0,
  output s2
);

  wire fulladder_2_c_out, fulladder_3_c_out, fulladder_4_c_out, fulladder_5_c_out;

  FullAdder fulladder_1 (.X(a4), .Y(b4), .C_IN(fulladder_2_c_out), .SUM(s4), .C_OUT(c4));
  FullAdder fulladder_2 (.X(a3), .Y(b3), .C_IN(fulladder_3_c_out), .SUM(s3), .C_OUT(fulladder_2_c_out));
  FullAdder fulladder_3 (.X(a2), .Y(b2), .C_IN(fulladder_4_c_out), .SUM(s2), .C_OUT(fulladder_3_c_out));
  FullAdder fulladder_4 (.X(a1), .Y(b1), .C_IN(fulladder_5_c_out), .SUM(s1), .C_OUT(fulladder_4_c_out));
  FullAdder fulladder_5 (.X(a0), .Y(b0), .C_IN(cin), .SUM(s0), .C_OUT(fulladder_5_c_out));
endmodule

// 5th bit
module _5th_Bit_Handler (
  input  fifthbit,
  input  s1,
  input  s2,
  output out_4
);

  wire xor_1_out;

  xor xor_1 (xor_1_out, fifthbit, s1);
  xor xor_2 (out_4, xor_1_out, s2);
endmodule

// Y/N
module Indicator (
  input  M,
  input  fifthbit,
  input  s1,
  input  s2,
  output indactor
);

  wire and_1_out, and_2_out, and_3_out, and_4_out, and_5_out, and_6_out, and_7_out, and_8_out, not_1_out,
       not_2_out, not_3_out, not_4_out, not_5_out, or_1_out, or_2_out;

  not not_1 (not_1_out, fifthbit);
  not not_2 (not_2_out, M);
  not not_3 (not_3_out, fifthbit);
  and and_1 (and_1_out, not_1_out, s1);
  not not_4 (not_4_out, s2);
  and and_2 (and_2_out, fifthbit, s1);
  and and_3 (and_3_out, M, fifthbit);
  not not_5 (not_5_out, s2);
  and and_4 (and_4_out, not_2_out, not_3_out);
  and and_5 (and_5_out, and_2_out, s2);
  and and_6 (and_6_out, and_3_out, not_5_out);
  and and_7 (and_7_out, and_4_out, s2);
  and and_8 (and_8_out, and_1_out, not_4_out);
  or or_1 (or_1_out, and_5_out, and_6_out);
  or or_2 (or_2_out, and_7_out, and_8_out);
  or or_3 (indactor, or_2_out, or_1_out);
endmodule

// Sign
module Sign_Handler (
  input  M,
  input  fifthbit,
  input  s1,
  input  s2,
  output signnn
);

  wire and_1_out, and_2_out, and_3_out, and_4_out, and_5_out, and_6_out, and_7_out, and_8_out, not_1_out,
       not_2_out, not_3_out, not_4_out, not_5_out, or_1_out, or_2_out;

  not not_1 (not_1_out, fifthbit);
  not not_2 (not_2_out, fifthbit);
  not not_3 (not_3_out, M);
  and and_1 (and_1_out, not_3_out, not_1_out);
  and and_2 (and_2_out, not_2_out, s1);
  not not_4 (not_4_out, s2);
  and and_3 (and_3_out, fifthbit, s1);
  and and_4 (and_4_out, M, fifthbit);
  not not_5 (not_5_out, s2);
  and and_5 (and_5_out, and_1_out, s2);
  or or_1 (or_1_out, and_5_out, and_6_out);
  and and_6 (and_6_out, and_2_out, not_4_out);
  and and_7 (and_7_out, and_3_out, s2);
  or or_2 (or_2_out, and_7_out, and_8_out);
  and and_8 (and_8_out, and_4_out, not_5_out);
  or or_3 (signnn, or_1_out, or_2_out);
endmodule
