// Logisim project Division-BCD TO 7 Segment.circ as structural Verilog: 7 circuits, main circuit 4-Bit Subtractor
module Divider (
  input  A4,
  input  A3,
  input  A2,
  input  A1,
  input  A0,
  input  B4,
  input  B3,
  input  B2,
  input  B1,
  input  B0,
  output Q4,
  output Q3,
  output Q2,
  output Q1,
  output Q0
);

  wire n4_bit_subtractor_1_s0, n4_bit_subtractor_1_s1, n4_bit_subtractor_1_s2, n4_bit_subtractor_2_s0,
       n4_bit_subtractor_2_s1, n4_bit_subtractor_2_s2, n4_bit_subtractor_3_s0, n4_bit_subtractor_3_s1,
       n4_bit_subtractor_3_s2, subtraction_fixer_1_out_10, subtraction_fixer_1_out_11,
       subtraction_fixer_1_out_12, subtraction_fixer_2_out_10, subtraction_fixer_2_out_11,
       subtraction_fixer_2_out_12, subtraction_fixer_3_out_10, subtraction_fixer_3_out_11,
       subtraction_fixer_3_out_12;

  Subtraction_Fixer subtraction_fixer_1 (
    .S2_OLD(subtraction_fixer_3_out_11), .S2_NEW(n4_bit_subtractor_2_s2), .Cout(Q2),
    .S1_OLD(subtraction_fixer_3_out_12), .S1_NEW(n4_bit_subtractor_2_s1), .Cout_2(Q2), .S0_OLD(A2),
    .S0_NEW(n4_bit_subtractor_2_s0), .Cout_3(Q2), .out_10(subtraction_fixer_1_out_10),
    .out_11(subtraction_fixer_1_out_11), .out_12(subtraction_fixer_1_out_12));
  Subtraction_Fixer subtraction_fixer_2 (
    .S2_OLD(subtraction_fixer_1_out_11), .S2_NEW(n4_bit_subtractor_3_s2), .Cout(Q1),
    .S1_OLD(subtraction_fixer_1_out_12), .S1_NEW(n4_bit_subtractor_3_s1), .Cout_2(Q1), .S0_OLD(A1),
    .S0_NEW(n4_bit_subtractor_3_s0), .Cout_3(Q1), .out_10(subtraction_fixer_2_out_10),
    .out_11(subtraction_fixer_2_out_11), .out_12(subtraction_fixer_2_out_12));
  _4_Bit_Subtractor u_4_bit_subtractor_1 (
    .A0(A3), .B0(B0), .A1(1'b0), .B1(B1), .A2(1'b0), .B2(B2), .A3(1'b0), .B3(B3),
    .S0(n4_bit_subtractor_1_s0), .S1(n4_bit_subtractor_1_s1), .S2(n4_bit_subtractor_1_s2), .Cout(Q3));  // open: S3
  Subtraction_Fixer subtraction_fixer_3 (
    .S2_OLD(1'b0), .S2_NEW(n4_bit_subtractor_1_s2), .Cout(Q3), .S1_OLD(1'b0),
    .S1_NEW(n4_bit_subtractor_1_s1), .Cout_2(Q3), .S0_OLD(A3), .S0_NEW(n4_bit_subtractor_1_s0), .Cout_3(Q3),
    .out_10(subtraction_fixer_3_out_10), .out_11(subtraction_fixer_3_out_11),
    .out_12(subtraction_fixer_3_out_12));
  _4_Bit_Subtractor u_4_bit_subtractor_2 (
    .A0(A2), .B0(B0), .A1(subtraction_fixer_3_out_12), .B1(B1), .A2(subtraction_fixer_3_out_11), .B2(B2),
    .A3(subtraction_fixer_3_out_10), .B3(B3), .S0(n4_bit_subtractor_2_s0), .S1(n4_bit_subtractor_2_s1),
    .S2(n4_bit_subtractor_2_s2), .Cout(Q2));  // open: S3
  _4_Bit_Subtractor u_4_bit_subtractor_3 (
    .A0(A1), .B0(B0), .A1(subtraction_fixer_1_out_12), .B1(B1), .A2(subtraction_fixer_1_out_11), .B2(B2),
    .A3(subtraction_fixer_1_out_10), .B3(B3), .S0(n4_bit_subtractor_3_s0), .S1(n4_bit_subtractor_3_s1),
    .S2(n4_bit_subtractor_3_s2), .Cout(Q1));  // open: S3
  _4_Bit_Subtractor u_4_bit_subtractor_4 (
    .A0(A0), .B0(B0), .A1(subtraction_fixer_2_out_12), .B1(B1), .A2(subtraction_fixer_2_out_11), .B2(B2),
    .A3(subtraction_fixer_2_out_10), .B3(B3), .Cout(Q0));  // open: S0, S1, S2, S3
  xor xor_1 (Q4, B4, A4);
endmodule

module _4_Bit_Subtractor (
  input  A0,
  input  B0,
  input  A1,
  input  B1,
  input  A2,
  input  B2,
  input  A3,
  input  B3,
  output Cout,
  output S0,
  output S1,
  output S2,
  output S3
);

  wire full_adder_1_cout, full_adder_2_cout, full_adder_3_cout, not_1_out, not_2_out, not_3_out, not_4_out;

  not not_1 (not_1_out, B0);
  Full_Adder full_adder_1 (.A(A0), .Cin(1'b1), .B(not_1_out), .Sum(S0), .Cout(full_adder_1_cout));
  Full_Adder full_adder_2 (.A(A1), .Cin(full_adder_1_cout), .B(not_2_out), .Sum(S1), .Cout(full_adder_2_cout));
  not not_2 (not_2_out, B1);
  not not_3 (not_3_out, B2);
  Full_Adder full_adder_3 (.A(A2), .Cin(full_adder_2_cout), .B(not_3_out), .Sum(S2), .Cout(full_adder_3_cout));
  not not_4 (not_4_out, B3);
  Full_Adder full_adder_4 (.A(A3), .Cin(full_adder_3_cout), .B(not_4_out), .Sum(S3), .Cout(Cout));

  // Notes on the sheet:
  //   Cin=1
endmodule

module Full_Adder (
  input  A,
  input  Cin,
  input  B,
  output Sum,
  output Cout
);

  wire half_adder_1_carry, half_adder_1_sum, half_adder_2_carry;

  Half_Adder half_adder_1 (.A(A), .B(B), .SUM(half_adder_1_sum), .Carry(half_adder_1_carry));
  Half_Adder half_adder_2 (.A(half_adder_1_sum), .B(Cin), .SUM(Sum), .Carry(half_adder_2_carry));
  or or_1 (Cout, half_adder_2_carry, half_adder_1_carry);

  // Notes on the sheet:
  //   Sum
  //   Cout
endmodule

module Half_Adder (
  input  A,
  input  B,
  output SUM,
  output Carry
);

  xor xor_1 (SUM, A, B);
  and and_1 (Carry, A, B);
endmodule

module Subtraction_Fixer (
  input  S2_OLD,
  input  S2_NEW,
  input  Cout,
  input  S1_OLD,
  input  S1_NEW,
  input  Cout_2,
  input  S0_OLD,
  input  S0_NEW,
  input  Cout_3,
  output out_10,
  output out_11,
  output out_12
);

  Multiplexer multiplexer_1 (.in0(S2_OLD), .in1(S2_NEW), .out(out_10), .sel(Cout), .en(1'b1));
  Multiplexer multiplexer_2 (.in0(S1_OLD), .in1(S1_NEW), .out(out_11), .sel(Cout_2), .en(1'b1));
  Multiplexer multiplexer_3 (.in0(S0_OLD), .in1(S0_NEW), .out(out_12), .sel(Cout_3), .en(1'b1));
endmodule

module BCD_TO_7_Segment (
  input  A,
  input  B,
  input  C,
  input  D,
  output a_2,
  output b_2,
  output c_2,
  output d_2,
  output e,
  output f,
  output g
);

  wire and_1_out, and_2_out, and_3_out, and_4_out, and_5_out, and_6_out, and_7_out, and_8_out, and_9_out,
       and_10_out, and_11_out, and_12_out, and_13_out, and_14_out, and_15_out, and_16_out, not_1_out,
       not_2_out, not_3_out, not_4_out, or_1_out, or_2_out, or_3_out, or_4_out, or_5_out, or_6_out, or_8_out,
       or_9_out, or_13_out, or_14_out;

  not not_1 (not_1_out, A);
  not not_2 (not_2_out, C);
  not not_3 (not_3_out, B);
  not not_4 (not_4_out, D);
  and and_1 (and_1_out, not_1_out, C);
  and and_2 (and_2_out, not_3_out, not_2_out);
  and and_3 (and_3_out, not_1_out, B);
  and and_4 (and_4_out, not_1_out, not_3_out);
  and and_5 (and_5_out, not_1_out, not_4_out);
  and and_6 (and_6_out, not_1_out, D);
  and and_7 (and_7_out, and_2_out, A);
  and and_8 (and_8_out, and_3_out, D);
  and and_9 (and_9_out, and_2_out, not_4_out);
  and and_10 (and_10_out, and_5_out, not_2_out);
  and and_11 (and_11_out, and_1_out, D);
  and and_12 (and_12_out, and_4_out, C);
  and and_13 (and_13_out, and_1_out, not_4_out);
  and and_14 (and_14_out, and_8_out, not_2_out);
  and and_15 (and_15_out, and_3_out, not_2_out);
  and and_16 (and_16_out, and_3_out, not_4_out);
  or or_1 (or_1_out, and_1_out, and_7_out);
  or or_2 (or_2_out, and_8_out, and_9_out);
  or or_3 (or_3_out, and_2_out, and_4_out);
  or or_4 (or_4_out, and_10_out, and_11_out);
  or or_5 (or_5_out, and_3_out, and_6_out);
  or or_6 (or_6_out, and_12_out, and_13_out);
  or or_7 (e, and_9_out, and_13_out);
  or or_8 (or_8_out, and_7_out, and_15_out);
  or or_9 (or_9_out, and_10_out, and_16_out);
  or or_10 (a_2, or_1_out, or_2_out);
  or or_11 (b_2, or_3_out, or_4_out);
  or or_12 (c_2, and_2_out, or_5_out);
  or or_13 (or_13_out, and_9_out, and_7_out);
  or or_14 (or_14_out, or_6_out, and_14_out);
  or or_15 (d_2, or_13_out, or_14_out);
  or or_16 (f, or_8_out, or_9_out);
  or or_17 (g, or_6_out, or_8_out);
endmodule

module Divide_by_Zero_Flag (
  input  in_1,
  input  in_2,
  input  in_3,
  input  in_4,
  output out_5
);

  wire or_1_out, or_2_out;

  or or_1 (or_1_out, in_1, in_2);
  or or_2 (or_2_out, in_3, in_4);
  nor nor_1 (out_5, or_1_out, or_2_out);
endmodule
