// Logisim project Multiplication-Binary to BCD.circ as structural Verilog: 8 circuits, main circuit Full Adder
module Main (
  input  A4,
  input  A3,
  input  A2,
  input  A1,
  input  A0,
  input  B4,
  input  B3,
  input  B2,
  input  B1,
  input  B0,
  output Sign,
  output H,
  output H_2,
  output T,
  output T_2,
  output T_3,
  output T_4,
  output U,
  output U_2,
  output U_3,
  output U_4
);

  wire multiplier_1_r0, multiplier_1_r1, multiplier_1_r2, multiplier_1_r3, multiplier_1_r4, multiplier_1_r5,
       multiplier_1_r6, multiplier_1_r7;

  Multiplier multiplier_1 (
    .A3(A3), .A2(A2), .A1(A1), .A0(A0), .B4(B4), .B3(B3), .B2(B2), .B1(B1), .B0(B0), .A4(A4),
    .R7(multiplier_1_r7), .R6(multiplier_1_r6), .R5(multiplier_1_r5), .R4(multiplier_1_r4),
    .R3(multiplier_1_r3), .R2(multiplier_1_r2), .R1(multiplier_1_r1), .R0(multiplier_1_r0), .Sign(Sign));
  binary_to_BCD_modified binary_to_bcd_modified_1 (
    .B7(multiplier_1_r7), .B6(multiplier_1_r6), .B5(multiplier_1_r5), .B4(multiplier_1_r4),
    .B3(multiplier_1_r3), .B2(multiplier_1_r2), .B1(multiplier_1_r1), .B0(multiplier_1_r0), .H(H), .H_2(H_2),
    .T(T), .T_2(T_2), .T_3(T_3), .T_4(T_4), .U(U), .U_2(U_2), .U_3(U_3), .U_4(U_4));
endmodule

module Full_Adder (
  input  in_1,
  input  in_2,
  input  in_3,
  output out_4,
  output C
);

  wire half_adder_1_out_3, half_adder_1_out_4, half_adder_2_out_4;

  Half_Adder half_adder_1 (.in_1(in_1), .in_2(in_3), .out_3(half_adder_1_out_3), .out_4(half_adder_1_out_4));
  Half_Adder half_adder_2 (.in_1(half_adder_1_out_3), .in_2(in_2), .out_3(out_4), .out_4(half_adder_2_out_4));
  or or_1 (C, half_adder_2_out_4, half_adder_1_out_4);
endmodule

module Half_Adder (
  input  in_1,
  input  in_2,
  output out_3,
  output out_4
);

  xor xor_1 (out_3, in_1, in_2);
  and and_1 (out_4, in_1, in_2);
endmodule

module _4_bit_binary_adder (
  input  B3,
  input  A3,
  input  B2,
  input  A2,
  input  B1,
  input  A1,
  input  B0,
  input  A0,
  output C3,
  output S3,
  output S2,
  output S1,
  output S0
);

  wire full_adder_2_c, full_adder_3_c, full_adder_4_c;

  Full_Adder full_adder_1 (.in_1(full_adder_2_c), .in_2(A3), .in_3(B3), .out_4(S3), .C(C3));
  Full_Adder full_adder_2 (.in_1(full_adder_3_c), .in_2(A2), .in_3(B2), .out_4(S2), .C(full_adder_2_c));
  Full_Adder full_adder_3 (.in_1(full_adder_4_c), .in_2(A1), .in_3(B1), .out_4(S1), .C(full_adder_3_c));
  Full_Adder full_adder_4 (.in_1(1'b0), .in_2(A0), .in_3(B0), .out_4(S0), .C(full_adder_4_c));
endmodule

module Multiplier (
  input  A4,
  input  A3,
  input  A2,
  input  A1,
  input  A0,
  input  B4,
  input  B3,
  input  B2,
  input  B1,
  input  B0,
  output R7,
  output R6,
  output R5,
  output R4,
  output R3,
  output R2,
  output R1,
  output R0,
  output Sign
);

  wire A0_B1_out, A0_B2_out, A0_B3_out, A1_B1_out, A1_B2_out, A1_B3_out, A1B0_out, A2_B0_out, A2_B1_out,
       A2_B2_out, A2_B3_out, A3_B0_out, A3_B1_out, A3_B2_out, A3_B3_out, n4_bit_binary_adder_2_c3,
       n4_bit_binary_adder_2_s1, n4_bit_binary_adder_2_s2, n4_bit_binary_adder_2_s3,
       n4_bit_binary_adder_3_c3, n4_bit_binary_adder_3_s1, n4_bit_binary_adder_3_s2, n4_bit_binary_adder_3_s3;

  and A3_B3 (A3_B3_out, A3, B3);
  and A3_B2 (A3_B2_out, A3, B2);
  and A3_B1 (A3_B1_out, A3, B1);
  and A3_B0 (A3_B0_out, A3, B0);
  and A2_B3 (A2_B3_out, A2, B3);
  and A2_B2 (A2_B2_out, A2, B2);
  and A2_B1 (A2_B1_out, A2, B1);
  and A2_B0 (A2_B0_out, A2, B0);
  and A1_B3 (A1_B3_out, A1, B3);
  _4_bit_binary_adder u_4_bit_binary_adder_1 (
    .B3(A3_B3_out), .A3(n4_bit_binary_adder_2_c3), .B2(A3_B2_out), .A2(n4_bit_binary_adder_2_s3),
    .B1(A3_B1_out), .A1(n4_bit_binary_adder_2_s2), .B0(A3_B0_out), .A0(n4_bit_binary_adder_2_s1), .C3(R7),
    .S3(R6), .S2(R5), .S1(R4), .S0(R3));
  and A1_B2 (A1_B2_out, A1, B2);
  and A1B0 (A1B0_out, A1, B0);
  and A1_B1 (A1_B1_out, A1, B1);
  _4_bit_binary_adder u_4_bit_binary_adder_2 (
    .B3(A2_B3_out), .A3(n4_bit_binary_adder_3_c3), .B2(A2_B2_out), .A2(n4_bit_binary_adder_3_s3),
    .B1(A2_B1_out), .A1(n4_bit_binary_adder_3_s2), .B0(A2_B0_out), .A0(n4_bit_binary_adder_3_s1),
    .C3(n4_bit_binary_adder_2_c3), .S3(n4_bit_binary_adder_2_s3), .S2(n4_bit_binary_adder_2_s2),
    .S1(n4_bit_binary_adder_2_s1), .S0(R2));
  _4_bit_binary_adder u_4_bit_binary_adder_3 (
    .B3(A1_B3_out), .A3(1'b0), .B2(A1_B2_out), .A2(A0_B3_out), .B1(A1_B1_out), .A1(A0_B2_out), .B0(A1B0_out),
    .A0(A0_B1_out), .C3(n4_bit_binary_adder_3_c3), .S3(n4_bit_binary_adder_3_s3),
    .S2(n4_bit_binary_adder_3_s2), .S1(n4_bit_binary_adder_3_s1), .S0(R1));
  and A0_B3 (A0_B3_out, A0, B3);
  and A0_B2 (A0_B2_out, A0, B2);
  and A0_B1 (A0_B1_out, A0, B1);
  and A0_B0 (R0, A0, B0);
  xor xor_1 (Sign, A4, B4);
endmodule

// Add-3 Circuit
module Add_3_circuit (
  input  A3,
  input  A2,
  input  A1,
  input  A0,
  output B3,
  output B2,
  output B1,
  output B0
);

  wire and_1_out, and_2_out, and_3_out, and_4_out, and_5_out, and_6_out, and_7_out, and_8_out, and_9_out,
       and_10_out, and_11_out, not_1_out, not_2_out, not_3_out, not_4_out, or_1_out, or_2_out, or_4_out;

  not not_1 (not_1_out, A3);
  not not_2 (not_2_out, A2);
  and and_1 (and_1_out, not_2_out, not_1_out);
  and and_2 (and_2_out, A2, A1);
  not not_3 (not_3_out, A1);
  not not_4 (not_4_out, A0);
  and and_3 (and_3_out, A1, A0);
  and and_4 (and_4_out, not_2_out, A1);
  and and_5 (and_5_out, and_1_out, A0);
  and and_6 (and_6_out, not_4_out, and_2_out);
  or or_1 (or_1_out, A1, A0);
  and and_7 (and_7_out, not_3_out, not_4_out);
  or or_2 (or_2_out, and_3_out, and_4_out);
  and and_8 (and_8_out, A3, not_4_out);
  or or_3 (B3, A3, and_9_out);
  and and_9 (and_9_out, A2, or_1_out);
  and and_10 (and_10_out, A3, A0);
  and and_11 (and_11_out, A2, and_7_out);
  or or_4 (or_4_out, and_8_out, and_5_out);
  or or_5 (B2, and_10_out, and_11_out);
  or or_6 (B1, or_2_out, and_8_out);
  or or_7 (B0, or_4_out, and_6_out);
endmodule

// Binary to BCD
module binary_to_BCD_modified (
  input  B7,
  input  B6,
  input  B5,
  input  B4,
  input  B3,
  input  B2,
  input  B1,
  input  B0,
  output H,
  output H_2,
  output T,
  output T_2,
  output T_3,
  output T_4,
  output U,
  output U_2,
  output U_3,
  output U_4
);

  wire add_3_circuit_1_b0, add_3_circuit_1_b1, add_3_circuit_1_b2, add_3_circuit_1_b3, add_3_circuit_2_b0,
       add_3_circuit_2_b1, add_3_circuit_2_b2, add_3_circuit_2_b3, add_3_circuit_3_b0, add_3_circuit_3_b1,
       add_3_circuit_3_b2, add_3_circuit_3_b3, add_3_circuit_4_b0, add_3_circuit_4_b1, add_3_circuit_4_b2,
       add_3_circuit_6_b0, add_3_circuit_6_b1, add_3_circuit_6_b2, add_3_circuit_6_b3;

  Add_3_circuit add_3_circuit_1 (
    .A3(1'b0), .A2(B7), .A1(B6), .A0(B5), .B3(add_3_circuit_1_b3), .B2(add_3_circuit_1_b2),
    .B1(add_3_circuit_1_b1), .B0(add_3_circuit_1_b0));
  Add_3_circuit add_3_circuit_2 (
    .A3(add_3_circuit_1_b2), .A2(add_3_circuit_1_b1), .A1(add_3_circuit_1_b0), .A0(B4),
    .B3(add_3_circuit_2_b3), .B2(add_3_circuit_2_b2), .B1(add_3_circuit_2_b1), .B0(add_3_circuit_2_b0));
  Add_3_circuit add_3_circuit_3 (
    .A3(add_3_circuit_2_b2), .A2(add_3_circuit_2_b1), .A1(add_3_circuit_2_b0), .A0(B3),
    .B3(add_3_circuit_3_b3), .B2(add_3_circuit_3_b2), .B1(add_3_circuit_3_b1), .B0(add_3_circuit_3_b0));
  Add_3_circuit add_3_circuit_4 (
    .A3(1'b0), .A2(add_3_circuit_1_b3), .A1(add_3_circuit_2_b3), .A0(add_3_circuit_3_b3), .B3(H),
    .B2(add_3_circuit_4_b2), .B1(add_3_circuit_4_b1), .B0(add_3_circuit_4_b0));
  Add_3_circuit add_3_circuit_5 (
    .A3(add_3_circuit_4_b2), .A2(add_3_circuit_4_b1), .A1(add_3_circuit_4_b0), .A0(add_3_circuit_6_b3),
    .B3(H_2), .B2(T), .B1(T_2), .B0(T_3));
  Add_3_circuit add_3_circuit_6 (
    .A3(add_3_circuit_3_b2), .A2(add_3_circuit_3_b1), .A1(add_3_circuit_3_b0), .A0(B2),
    .B3(add_3_circuit_6_b3), .B2(add_3_circuit_6_b2), .B1(add_3_circuit_6_b1), .B0(add_3_circuit_6_b0));
  Add_3_circuit add_3_circuit_7 (
    .A3(add_3_circuit_6_b2), .A2(add_3_circuit_6_b1), .A1(add_3_circuit_6_b0), .A0(B1), .B3(T_4), .B2(U),
    .B1(U_2), .B0(U_3));

  assign U_4 = B0;
endmodule

module Zero_Flag (
  input  in_1,
  input  in_2,
  input  in_3,
  input  in_4,
  input  in_5,
  input  in_6,
  input  in_7,
  input  in_8,
  output out_9
);

  wire or_1_out, or_2_out, or_3_out, or_4_out, or_5_out, or_6_out;

  or or_1 (or_1_out, in_1, in_2);
  or or_2 (or_2_out, in_3, in_4);
  or or_3 (or_3_out, in_5, in_6);
  or or_4 (or_4_out, in_7, in_8);
  or or_5 (or_5_out, or_1_out, or_2_out);
  or or_6 (or_6_out, or_3_out, or_4_out);
  nor nor_1 (out_9, or_5_out, or_6_out);
endmodule
