// Logisim project PROJECT.circ as structural Verilog: 3 circuits, main circuit Calculator
module ALU (
  input  A4,
  input  A3,
  input  A2,
  input  A1,
  input  A0,
  input  B4,
  input  B3,
  input  B2,
  input  B1,
  input  B0,
  input  [1:0] Mode,
  output Div_by_Zero_Flag,
  output Sign,
  output R7,
  output R6,
  output R5,
  output R4,
  output R3,
  output R2,
  output R1,
  output R0,
  output Zero_Flag
);

  wire adder_subtractor_1_r0, adder_subtractor_1_r1, adder_subtractor_1_r2, adder_subtractor_1_r3,
       adder_subtractor_1_r4, adder_subtractor_1_sign, divide_by_zero_flag_1_out_5, divider_1_q0,
       divider_1_q1, divider_1_q2, divider_1_q3, divider_1_q4, multiplier_1_r0, multiplier_1_r1,
       multiplier_1_r2, multiplier_1_r3, multiplier_1_r4, multiplier_1_r5, multiplier_1_r6, multiplier_1_r7,
       multiplier_1_sign;

  _4x1_MUX u_4x1_mux_1 (
    .A___S(adder_subtractor_1_sign), .A___S_2(adder_subtractor_1_sign), .M(multiplier_1_sign),
    .D(divider_1_q4), .Bit_1(Mode[1]), .Bit_0(Mode[0]), .out_7(Sign));
  _4x1_MUX u_4x1_mux_2 (
    .A___S(1'b0), .A___S_2(1'b0), .M(multiplier_1_r7), .D(1'b0), .Bit_1(Mode[1]), .Bit_0(Mode[0]), .out_7(R7));
  _4x1_MUX u_4x1_mux_3 (
    .A___S(1'b0), .A___S_2(1'b0), .M(multiplier_1_r6), .D(1'b0), .Bit_1(Mode[1]), .Bit_0(Mode[0]), .out_7(R6));
  _4x1_MUX u_4x1_mux_4 (
    .A___S(1'b0), .A___S_2(1'b0), .M(multiplier_1_r5), .D(1'b0), .Bit_1(Mode[1]), .Bit_0(Mode[0]), .out_7(R5));
  _4x1_MUX u_4x1_mux_5 (
    .A___S(adder_subtractor_1_r4), .A___S_2(adder_subtractor_1_r4), .M(multiplier_1_r4), .D(1'b0),
    .Bit_1(Mode[1]), .Bit_0(Mode[0]), .out_7(R4));
  Adder__Subtractor adder_subtractor_1 (
    ._0__Add(Mode[0]), .Sign(adder_subtractor_1_sign), .B4(B4), .B3(B3), .B2(B2), .B1(B1), .B0(B0), .A4(A4),
    .A3(A3), .A2(A2), .A1(A1), .A0(A0), .R4(adder_subtractor_1_r4), .R3(adder_subtractor_1_r3),
    .R2(adder_subtractor_1_r2), .R1(adder_subtractor_1_r1), .R0(adder_subtractor_1_r0));
  Multiplier multiplier_1 (
    .A3(A3), .A2(A2), .A1(A1), .A0(A0), .B4(B4), .B3(B3), .B2(B2), .B1(B1), .B0(B0), .A4(A4),
    .R7(multiplier_1_r7), .R6(multiplier_1_r6), .R5(multiplier_1_r5), .R4(multiplier_1_r4),
    .R3(multiplier_1_r3), .R2(multiplier_1_r2), .R1(multiplier_1_r1), .R0(multiplier_1_r0),
    .Sign(multiplier_1_sign));
  Divider divider_1 (
    .A4(A4), .A3(A3), .A2(A2), .A1(A1), .A0(A0), .B4(B4), .B3(B3), .B2(B2), .B1(B1), .B0(B0),
    .Q4(divider_1_q4), .Q3(divider_1_q3), .Q2(divider_1_q2), .Q1(divider_1_q1), .Q0(divider_1_q0));
  Zero_Flag zero_flag_1 (
    .in_1(R0), .in_2(R1), .in_3(R2), .in_4(R3), .in_5(R4), .in_6(R5), .in_7(R6), .in_8(R7), .out_9(Zero_Flag));
  _4x1_MUX u_4x1_mux_6 (
    .A___S(adder_subtractor_1_r3), .A___S_2(adder_subtractor_1_r3), .M(multiplier_1_r3), .D(divider_1_q3),
    .Bit_1(Mode[1]), .Bit_0(Mode[0]), .out_7(R3));
  Divide_by_Zero_Flag divide_by_zero_flag_1 (
    .in_1(B3), .in_2(B2), .in_3(B1), .in_4(B0), .out_5(divide_by_zero_flag_1_out_5));
  _4x1_MUX u_4x1_mux_7 (
    .A___S(adder_subtractor_1_r2), .A___S_2(adder_subtractor_1_r2), .M(multiplier_1_r2), .D(divider_1_q2),
    .Bit_1(Mode[1]), .Bit_0(Mode[0]), .out_7(R2));
  Multiplexer multiplexer_1 (
    .in0(1'b0), .in1(divide_by_zero_flag_1_out_5), .out(Div_by_Zero_Flag), .sel(Mode[0]), .en(Mode[1]));
  _4x1_MUX u_4x1_mux_8 (
    .A___S(adder_subtractor_1_r1), .A___S_2(adder_subtractor_1_r1), .M(multiplier_1_r1), .D(divider_1_q1),
    .Bit_1(Mode[1]), .Bit_0(Mode[0]), .out_7(R1));
  _4x1_MUX u_4x1_mux_9 (
    .A___S(adder_subtractor_1_r0), .A___S_2(adder_subtractor_1_r0), .M(multiplier_1_r0), .D(divider_1_q0),
    .Bit_1(Mode[1]), .Bit_0(Mode[0]), .out_7(R0));

  // Notes on the sheet:
  //   Zero Flag
  //   Div by Zero Flag
endmodule

module _4x1_MUX (
  input  A___S,
  input  A___S_2,
  input  M,
  input  D,
  input  Bit_1,
  input  Bit_0,
  output out_7
);

  wire and_1_out, and_2_out, and_3_out, and_4_out, and_5_out, and_6_out, and_7_out, and_8_out, not_1_out,
       not_2_out, or_1_out, or_2_out;

  not not_1 (not_1_out, Bit_1);
  not not_2 (not_2_out, Bit_0);
  and and_1 (and_1_out, A___S, not_2_out);
  and and_2 (and_2_out, and_1_out, not_1_out);
  and and_3 (and_3_out, A___S_2, not_1_out);
  and and_4 (and_4_out, and_3_out, Bit_0);
  and and_5 (and_5_out, M, Bit_1);
  and and_6 (and_6_out, and_5_out, not_2_out);
  and and_7 (and_7_out, D, Bit_1);
  and and_8 (and_8_out, and_7_out, Bit_0);
  or or_1 (or_1_out, and_2_out, and_4_out);
  or or_2 (or_2_out, and_6_out, and_8_out);
  or or_3 (out_7, or_1_out, or_2_out);
endmodule

module Calculator (
  input  A4,
  input  A3,
  input  A2,
  input  A1,
  input  A0,
  input  B4,
  input  B3,
  input  B2,
  input  B1,
  input  B0,
  input  [1:0] Mode
);

  wire alu_1_div_by_zero_flag, alu_1_r0, alu_1_r1, alu_1_r2, alu_1_r3, alu_1_r4, alu_1_r5, alu_1_r6,
       alu_1_r7, alu_1_sign, alu_1_zero_flag, bcd_to_7_segment_1_a_2, bcd_to_7_segment_1_b_2,
       bcd_to_7_segment_1_c_2, bcd_to_7_segment_1_d_2, bcd_to_7_segment_1_e, bcd_to_7_segment_1_f,
       bcd_to_7_segment_1_g, bcd_to_7_segment_2_a_2, bcd_to_7_segment_2_b_2, bcd_to_7_segment_2_c_2,
       bcd_to_7_segment_2_d_2, bcd_to_7_segment_2_e, bcd_to_7_segment_2_f, bcd_to_7_segment_2_g,
       bcd_to_7_segment_3_a_2, bcd_to_7_segment_3_b_2, bcd_to_7_segment_3_c_2, bcd_to_7_segment_3_d_2,
       bcd_to_7_segment_3_e, bcd_to_7_segment_3_f, bcd_to_7_segment_3_g, binary_to_bcd_modified_1_h,
       binary_to_bcd_modified_1_h_2, binary_to_bcd_modified_1_t, binary_to_bcd_modified_1_t_2,
       binary_to_bcd_modified_1_t_3, binary_to_bcd_modified_1_t_4, binary_to_bcd_modified_1_u,
       binary_to_bcd_modified_1_u_2, binary_to_bcd_modified_1_u_3, binary_to_bcd_modified_1_u_4;

  LED led_1 (.in(alu_1_sign));
  LED led_2 (.in(alu_1_zero_flag));
  LED led_3 (.in(alu_1_div_by_zero_flag));
  ALU alu_1 (
    .Mode(Mode), .A4(A4), .A3(A3), .A2(A2), .A1(A1), .A0(A0), .B4(B4), .B3(B3), .B2(B2), .B1(B1), .B0(B0),
    .Sign(alu_1_sign), .R7(alu_1_r7), .R6(alu_1_r6), .R5(alu_1_r5), .R4(alu_1_r4), .R3(alu_1_r3),
    .R2(alu_1_r2), .R1(alu_1_r1), .R0(alu_1_r0), .Div_by_Zero_Flag(alu_1_div_by_zero_flag),
    .Zero_Flag(alu_1_zero_flag));
  binary_to_BCD_modified binary_to_bcd_modified_1 (
    .B7(alu_1_r7), .B6(alu_1_r6), .B5(alu_1_r5), .B4(alu_1_r4), .B3(alu_1_r3), .B2(alu_1_r2), .B1(alu_1_r1),
    .B0(alu_1_r0), .H(binary_to_bcd_modified_1_h), .H_2(binary_to_bcd_modified_1_h_2),
    .T(binary_to_bcd_modified_1_t), .T_2(binary_to_bcd_modified_1_t_2), .T_3(binary_to_bcd_modified_1_t_3),
    .T_4(binary_to_bcd_modified_1_t_4), .U(binary_to_bcd_modified_1_u), .U_2(binary_to_bcd_modified_1_u_2),
    .U_3(binary_to_bcd_modified_1_u_3), .U_4(binary_to_bcd_modified_1_u_4));
  BCD_TO_7_Segment bcd_to_7_segment_1 (
    .a_2(bcd_to_7_segment_1_a_2), .b_2(bcd_to_7_segment_1_b_2), .c_2(bcd_to_7_segment_1_c_2),
    .d_2(bcd_to_7_segment_1_d_2), .e(bcd_to_7_segment_1_e), .f(bcd_to_7_segment_1_f),
    .g(bcd_to_7_segment_1_g), .A(binary_to_bcd_modified_1_u), .B(binary_to_bcd_modified_1_u_2),
    .C(binary_to_bcd_modified_1_u_3), .D(binary_to_bcd_modified_1_u_4));
  BCD_TO_7_Segment bcd_to_7_segment_2 (
    .a_2(bcd_to_7_segment_2_a_2), .b_2(bcd_to_7_segment_2_b_2), .c_2(bcd_to_7_segment_2_c_2),
    .d_2(bcd_to_7_segment_2_d_2), .e(bcd_to_7_segment_2_e), .f(bcd_to_7_segment_2_f),
    .g(bcd_to_7_segment_2_g), .A(binary_to_bcd_modified_1_t), .B(binary_to_bcd_modified_1_t_2),
    .C(binary_to_bcd_modified_1_t_3), .D(binary_to_bcd_modified_1_t_4));
  BCD_TO_7_Segment bcd_to_7_segment_3 (
    .a_2(bcd_to_7_segment_3_a_2), .b_2(bcd_to_7_segment_3_b_2), .c_2(bcd_to_7_segment_3_c_2),
    .d_2(bcd_to_7_segment_3_d_2), .e(bcd_to_7_segment_3_e), .f(bcd_to_7_segment_3_f),
    .g(bcd_to_7_segment_3_g), .A(1'b0), .B(1'b0), .C(binary_to_bcd_modified_1_h),
    .D(binary_to_bcd_modified_1_h_2));
  _7_Segment_Display u_7_segment_display_1 (
    .g(bcd_to_7_segment_3_g), .f(bcd_to_7_segment_3_f), .a(bcd_to_7_segment_3_a_2),
    .b(bcd_to_7_segment_3_b_2), .e(bcd_to_7_segment_3_e), .d(bcd_to_7_segment_3_d_2),
    .c(bcd_to_7_segment_3_c_2));  // open: dp
  _7_Segment_Display u_7_segment_display_2 (
    .g(bcd_to_7_segment_2_g), .f(bcd_to_7_segment_2_f), .a(bcd_to_7_segment_2_a_2),
    .b(bcd_to_7_segment_2_b_2), .e(bcd_to_7_segment_2_e), .d(bcd_to_7_segment_2_d_2),
    .c(bcd_to_7_segment_2_c_2));  // open: dp
  _7_Segment_Display u_7_segment_display_3 (
    .g(bcd_to_7_segment_1_g), .f(bcd_to_7_segment_1_f), .a(bcd_to_7_segment_1_a_2),
    .b(bcd_to_7_segment_1_b_2), .e(bcd_to_7_segment_1_e), .d(bcd_to_7_segment_1_d_2),
    .c(bcd_to_7_segment_1_c_2));  // open: dp

  // Notes on the sheet:
  //   Sign Flag
  //   Zero Flag
  //   Div by Zero Flag
  //   Mode Menu
  //   For Addition :       00
  //   For Subtraction:   01
  //   For Multiplication: 10
  //   For Division:         11
endmodule
